# Fritzing sketch branchement_bouton (saved by Fritzing 0.9.10b)
breadboards: 1

parts:
  Part1 = Arduino Mega 2560 (Rev3)
  LED2 = smd LED [color="Red (633nm)" package="0805 [SMD]"]
  R2 = Resistor [tolerance=±5% power=0.25 resistance=220 package=THT]
  S2 = Pushbutton [package="[THT]"]

nets:
  N1: Part1.GND, LED2.cathode, S2.Pin_1, S2.Pin_2
  N2: Part1.D9_PWM, R2.Pin_1
  N3: Part1.D2_PWM, S2.Pin_3, S2.Pin_4
  N4: LED2.anode, R2.Pin_0
