# Fritzing sketch branchement_lcd (saved by Fritzing 0.9.9b)
breadboards: 1

parts:
  Part1 = Arduino Mega 2560 (Rev3)
  LCD1 = LCD screen

nets:
  GND: Part1.GND, LCD1.VSS, LCD1.R/W, LCD1.LED-
  5V: Part1.5V, LCD1.VDD, LCD1.LED+
  N1: Part1.D26, LCD1.DB7
  N2: Part1.D28, LCD1.DB6
  N3: Part1.D30, LCD1.DB5
  N4: Part1.D32, LCD1.DB4
  N5: Part1.D34, LCD1.E
  N6: Part1.D36, LCD1.RS
  N7: Part1.D38, LCD1.V0
