# Fritzing sketch branchement_led (saved by Fritzing 0.9.10b)
breadboards: 1

parts:
  Part1 = Arduino Mega 2560 (Rev3)
  LED2 = smd LED [color="Red (633nm)" package="0805 [SMD]"]
  R2 = Resistor [tolerance=±5% power=0.25 resistance=220 package=THT]

nets:
  N1: Part1.GND, LED2.cathode
  N2: Part1.D9_PWM, R2.Pin_1
  N3: LED2.anode, R2.Pin_0
