# Fritzing sketch dht11 (saved by Fritzing 0.9.9b)
breadboards: 1

parts:
  Part1 = Arduino Mega 2560 (Rev3)
  J2 = male pin header, 3 pins [form="♂ (male)"]

nets:
  N1: Part1.GND, J2.pin1
  N2: Part1.5V, J2.pin3
  N3: Part1.D2_PWM, J2.pin2
