# Fritzing sketch photoresistance (saved by Fritzing 0.9.10b)
breadboards: 1

parts:
  Part1 = Arduino Mega 2560 (Rev3)
  R1 = PHOTOCELL [package=photocell-kit]
  R2 = Resistor [tolerance=±5% power=0.25 resistance=10k package=THT]

nets:
  N1: Part1.A0, R1.P$2, R2.Pin_0
  N2: Part1.GND, R2.Pin_1
  N3: Part1.5V, R1.P$1
